// Logisim project oblArqui.circ as structural Verilog: 2 circuits, main circuit main
module main (
);

  wire button_1_out, button_2_out, button_3_out, clock_1_out, clock_2_out, d_ff_1_q, decoder_1_out1,
       decoder_1_out2, decoder_1_out3, decoder_1_out4, decoder_1_out5;
  wire [2:0] undriven;
  wire [3:0] contadorreloj_1_mins, contadorreloj_1_segs, contadorreloj_1_segs2;
  wire [7:0] shift_register_1_q7, shift_register_2_q7, shift_register_3_q7, shift_register_4_q7,
       shift_register_5_q7;

  Decoder #(.select(3)) decoder_1 (
    .out1(decoder_1_out1), .out2(decoder_1_out2), .out3(decoder_1_out3), .out4(decoder_1_out4),
    .out5(decoder_1_out5), .sel(undriven));  // open: out0, out6, out7, en
  Random #(.width(3)) random_1 ();  // open: clk, next, out, clr
  Clock clock_1 (.out(clock_1_out));
  Shift_Register shift_register_1 (
    .in(decoder_1_out1), .clk(clock_1_out), .q0(shift_register_1_q7[7]), .q1(shift_register_1_q7[6]),
    .q2(shift_register_1_q7[5]), .q3(shift_register_1_q7[4]), .q4(shift_register_1_q7[3]),
    .q5(shift_register_1_q7[2]), .q6(shift_register_1_q7[1]), .q7(shift_register_1_q7[0]));  // open: shift, out, load, clr, d0, d1, d2, d3, d4, d5, d6, d7
  Shift_Register shift_register_2 (
    .in(decoder_1_out2), .clk(clock_1_out), .q0(shift_register_2_q7[7]), .q1(shift_register_2_q7[6]),
    .q2(shift_register_2_q7[5]), .q3(shift_register_2_q7[4]), .q4(shift_register_2_q7[3]),
    .q5(shift_register_2_q7[2]), .q6(shift_register_2_q7[1]), .q7(shift_register_2_q7[0]));  // open: shift, out, load, clr, d0, d1, d2, d3, d4, d5, d6, d7
  Shift_Register shift_register_3 (
    .in(decoder_1_out3), .clk(clock_1_out), .q0(shift_register_3_q7[7]), .q1(shift_register_3_q7[6]),
    .q2(shift_register_3_q7[5]), .q3(shift_register_3_q7[4]), .q4(shift_register_3_q7[3]),
    .q5(shift_register_3_q7[2]), .q6(shift_register_3_q7[1]), .q7(shift_register_3_q7[0]));  // open: shift, out, load, clr, d0, d1, d2, d3, d4, d5, d6, d7
  Shift_Register shift_register_4 (
    .in(decoder_1_out4), .clk(clock_1_out), .q0(shift_register_4_q7[7]), .q1(shift_register_4_q7[6]),
    .q2(shift_register_4_q7[5]), .q3(shift_register_4_q7[4]), .q4(shift_register_4_q7[3]),
    .q5(shift_register_4_q7[2]), .q6(shift_register_4_q7[1]), .q7(shift_register_4_q7[0]));  // open: shift, out, load, clr, d0, d1, d2, d3, d4, d5, d6, d7
  Shift_Register shift_register_5 (
    .in(decoder_1_out5), .clk(clock_1_out), .q0(shift_register_5_q7[7]), .q1(shift_register_5_q7[6]),
    .q2(shift_register_5_q7[5]), .q3(shift_register_5_q7[4]), .q4(shift_register_5_q7[3]),
    .q5(shift_register_5_q7[2]), .q6(shift_register_5_q7[1]), .q7(shift_register_5_q7[0]));  // open: shift, out, load, clr, d0, d1, d2, d3, d4, d5, d6, d7
  Button button_1 (.out(button_1_out));
  D_Flip_Flop d_ff_1 (.Q(d_ff_1_q), .preset(button_1_out), .reset(button_2_out));  // open: D, clk, Qn
  Button button_2 (.out(button_2_out));
  Clock clock_2 (.out(clock_2_out));
  DotMatrix #(.matrixrows(1)) dotmatrix_1 (
    .col0(decoder_1_out1), .col1(decoder_1_out2), .col2(decoder_1_out3), .col3(decoder_1_out4),
    .col4(decoder_1_out5));
  DotMatrix #(.matrixrows(8)) dotmatrix_2 (
    .col0(shift_register_1_q7), .col1(shift_register_2_q7), .col2(shift_register_3_q7),
    .col3(shift_register_4_q7), .col4(shift_register_5_q7));
  // AND_Gate and_1 has open pins: in0=d_ff_1_q, in1=clock_2_out, out=open
  Button button_3 (.out(button_3_out));
  contadorReloj contadorreloj_1 (
    .Mins(contadorreloj_1_mins), .Segs2(contadorreloj_1_segs2), .Segs(contadorreloj_1_segs),
    .Reset(button_3_out));  // open: in_1
  Hex_Digit_Display hex_digit_display_1 (.value(contadorreloj_1_mins));  // open: dp
  Hex_Digit_Display hex_digit_display_2 (.value(contadorreloj_1_segs2));  // open: dp
  Hex_Digit_Display hex_digit_display_3 (.value(contadorreloj_1_segs));  // open: dp
endmodule

module contadorReloj (
  input  in_1,
  output [3:0] Mins,
  output [3:0] Segs2,
  output [3:0] Segs,
  output Reset
);

  wire and_1_out, clock_1_out, counter_2_carry, counter_3_carry, d_ff_1_q;

  D_Flip_Flop d_ff_1 (.Q(d_ff_1_q), .preset(in_1), .reset(Reset));  // open: D, clk, Qn
  Clock clock_1 (.out(clock_1_out));
  and and_1 (and_1_out, d_ff_1_q, clock_1_out);
  Counter #(.max('h2), .trigger("falling"), .width(4)) counter_1 (
    .clr(Reset), .clk(counter_2_carry), .carry(Reset), .Q(Mins));  // open: load, up, count, D
  Counter #(.max('h5), .trigger("falling"), .width(4)) counter_2 (
    .clr(Reset), .clk(counter_3_carry), .carry(counter_2_carry), .Q(Segs2));  // open: load, up, count, D
  Counter #(.max('h9), .width(4)) counter_3 (
    .clr(Reset), .clk(and_1_out), .carry(counter_3_carry), .Q(Segs));  // open: load, up, count, D
endmodule
